# Fritzing sketch allskypi (saved by Fritzing 0.9.8b)
breadboards: 1

parts:
  Raspberry_Pi1 = Raspberry Pi B+
  R1 = Resistor [tolerance=±5% power=0.25 resistance=4.7k package=THT]
  Fan = Fan - Ventilador [package=THT]
  Humidity_and_Temperature_Sensor_DHT22 = Humidity and Temperature Sensor RHT03
  Relay_5V1 = Keyes Relay [package=THT]

nets (from the schematic view):
  3V3: Raspberry_Pi1.3v3, R1.Pin_1, Humidity_and_Temperature_Sensor_DHT22.Vcc
  N1: Raspberry_Pi1.GPIO4, R1.Pin_0, Humidity_and_Temperature_Sensor_DHT22.Data-signal
  GND: Raspberry_Pi1.GND, Fan.GND, Humidity_and_Temperature_Sensor_DHT22.GND_1, Relay_5V1.ground
  N2: Raspberry_Pi1.GPIO23, Relay_5V1.signal
  N3: Raspberry_Pi1.5V, Relay_5V1.NC, Relay_5V1.C, Relay_5V1.NO
  N4: Fan.5V, Relay_5V1.power

custom parts:
  Fan - Ventilador: Ventilador de 2 pines, se encuentra comunmente en computadoras de escritorio
  Keyes Relay: The Keyes 5V relay module is suitable for SCM development, home appliance control. It uses a 5V~12V TIL control signal which can control DC / AC signal.
